// Logisim project CPU.circ as structural Verilog: 12 circuits, main circuit main
module main (
  output [3:0] out_1
);

  wire ADD, Clear, CLK, controlled_buffer_1_out, not_1_out, or_1_out, or_2_out, s_r_ff_1_q;
  wire [1:0] Addr_1, Addr_2, multiplexer_1_out;
  wire [4:0] PROGRAM_COUNTER_out_2;
  wire [4:1] connect;
  wire [7:0] alu_1_y, demux_1_alu, demux_1_memory, demux_1_reg, mux_2_1_out, ram_1_data, register_2_q,
       register_bank_1_out_1, register_bank_1_out_2, rom_1_data;
  wire [7:4] register_1_q;

  Clock clock_1 (.out(CLK));
  assign controlled_buffer_1_out = not_1_out ? CLK : 1'bz;  // Controlled_Buffer controlled_buffer_1
  not not_1 (not_1_out, s_r_ff_1_q);
  Multiplexer #(.width(2)) multiplexer_1 (
    .in0(Addr_1), .in1(Addr_2), .out(multiplexer_1_out), .sel(connect[4]));  // open: en
  Program_Counter PROGRAM_COUNTER (.in_1(controlled_buffer_1_out), .out_2(PROGRAM_COUNTER_out_2));
  S_R_Flip_Flop s_r_ff_1 (.S(Clear), .clk(CLK), .R(1'b0), .Q(s_r_ff_1_q));  // open: Qn, preset, reset, en
  or or_1 (or_1_out, connect[4], connect[3]);
  RAM #(.addrWidth(2), .bus("separate")) ram_1 (
    .addr(multiplexer_1_out), .din(demux_1_memory), .data(ram_1_data), .str(connect[4]), .sel(or_1_out),
    .clk(CLK), .ld(connect[3]));  // open: clr
  ROM #(.addrWidth(5)) rom_1 (.addr(PROGRAM_COUNTER_out_2), .data(rom_1_data));  // open: sel
  Register register_1 (.D(rom_1_data), .Q({register_1_q, Addr_2, Addr_1}), .clk(CLK));  // open: en, clr
  Mux_2 mux_2_1 (.ALU(register_2_q), .Reg(demux_1_reg), .Memory(ram_1_data), .in_4({connect, ADD}), .out(mux_2_1_out));
  and u_ADD (ADD, register_1_q[7], ~register_1_q[6], ~register_1_q[5], register_1_q[4]);  // AND_Gate
  and Ry2Rx (connect[1], register_1_q[7], ~register_1_q[6], register_1_q[5], register_1_q[4]);  // AND_Gate
  and Ra2Rx (connect[2], register_1_q[7], register_1_q[6], ~register_1_q[5], ~register_1_q[4]);  // AND_Gate
  and Mem2Rx (connect[3], register_1_q[7], register_1_q[6], ~register_1_q[5], register_1_q[4]);  // AND_Gate
  and Rx2Mem (connect[4], register_1_q[7], register_1_q[6], register_1_q[5], ~register_1_q[4]);  // AND_Gate
  and HLT (Clear, register_1_q[7], ~register_1_q[6], ~register_1_q[5], ~register_1_q[4]);  // AND_Gate
  or or_2 (or_2_out, connect[3], connect[1], connect[2]);
  Register_Bank register_bank_1 (
    .write(or_2_out), .val_in(mux_2_1_out), .Addr_3(Addr_2), .out_1(register_bank_1_out_1), .Addr_1(Addr_1),
    .out_2(register_bank_1_out_2), .Addr_2(Addr_2));
  demux demux_1 (
    .in(register_bank_1_out_1), .in_2({connect, ADD}), .ALU(demux_1_alu), .Reg(demux_1_reg),
    .Memory(demux_1_memory));
  Mux mux_1 (.opcode(out_1), .Addr_in({{5{1'b0}}, ADD}));
  ALU alu_1 (.opcode_in(out_1), .a(demux_1_alu), .b(register_bank_1_out_2), .Y(alu_1_y));  // open: overflow, Carry_Flag
  Register register_2 (.D(alu_1_y), .Q(register_2_q), .clk(CLK));  // open: en, clr
  // NOT_Gate not_2 is placed but not wired

  // Other names for the same wires on the sheet: connect[0] = ADD; Copy = connect[1]; Copy_A = connect[2];
  //   Load_M = connect[3]; Load_2_M = connect[4]; opcode[3:0] = out_1

  // Notes on the sheet:
  //   CPU Clock
  //   RAM
  //   INSTRUCTION MEMORY
  //   contents of rom_1 (hex, n*v repeats v):
  //   d0 d5 da df 91 c0 98 c0 9c c0 e0 80
  //   DECODER
  //   Accumulator
endmodule

module ALU (
  input  [3:0] opcode_in,
  input  [7:0] a,
  input  [7:0] b,
  output overflow,
  output [7:0] Y,
  output Carry_Flag
);

  wire [7:0] Arithmetic_Unit_y, Logic_Unit_y, multiplexer_1_out, multiplexer_2_out, not_1_out, not_2_out;

  assign not_1_out = ~a;  // NOT_Gate not_1, 8 bits wide
  assign not_2_out = ~b;  // NOT_Gate not_2, 8 bits wide
  Multiplexer #(.width(8)) multiplexer_1 (
    .in0(a), .in1(not_1_out), .out(multiplexer_1_out), .sel(opcode_in[0]));  // open: en
  Multiplexer #(.width(8)) multiplexer_2 (
    .in0(b), .in1(not_2_out), .out(multiplexer_2_out), .sel(opcode_in[1]));  // open: en
  AU Arithmetic_Unit (
    .cin(opcode_in[2]), .a(multiplexer_1_out), .b(multiplexer_2_out), .Y(Arithmetic_Unit_y),
    .overflow(overflow), .cout(Carry_Flag));
  LU Logic_Unit (.a(a), .b(multiplexer_2_out), .y(Logic_Unit_y), .f2(opcode_in[2]), .f0(opcode_in[0]));
  Multiplexer #(.width(8)) multiplexer_3 (
    .in0(Arithmetic_Unit_y), .in1(Logic_Unit_y), .out(Y), .sel(opcode_in[3]));  // open: en

  // Other names for the same wires on the sheet: f0 = opcode_in[0]; f1 = opcode_in[1]; f2 = opcode_in[2];
  //   f3 = opcode_in[3]
endmodule

module Program_Counter (
  input  in_1,
  output [4:0] out_2
);

  Counter #(.width(5), .max('h1f)) counter_1 (.count(1'b1), .Q(out_2), .clk(in_1));  // open: load, D, carry, clr
endmodule

module AU (
  input  cin,
  input  [7:0] a,
  input  [7:0] b,
  output [7:0] Y,
  output overflow,
  output cout
);

  wire adder_1_cout, adder_2_cout, adder_3_cout, adder_4_cout, adder_5_cout, adder_6_cout, adder_7_cout;

  Adder #(.width(1)) adder_1 (.a(a[0]), .b(b[0]), .out(Y[0]), .cin(cin), .cout(adder_1_cout));
  Adder #(.width(1)) adder_2 (.a(a[1]), .b(b[1]), .out(Y[1]), .cin(adder_1_cout), .cout(adder_2_cout));
  Adder #(.width(1)) adder_3 (.a(a[2]), .b(b[2]), .out(Y[2]), .cin(adder_2_cout), .cout(adder_3_cout));
  Adder #(.width(1)) adder_4 (.a(a[3]), .b(b[3]), .out(Y[3]), .cin(adder_3_cout), .cout(adder_4_cout));
  Adder #(.width(1)) adder_5 (.a(a[4]), .b(b[4]), .out(Y[4]), .cin(adder_4_cout), .cout(adder_5_cout));
  Adder #(.width(1)) adder_6 (.a(a[5]), .b(b[5]), .out(Y[5]), .cin(adder_5_cout), .cout(adder_6_cout));
  Adder #(.width(1)) adder_7 (.a(a[6]), .b(b[6]), .out(Y[6]), .cin(adder_6_cout), .cout(adder_7_cout));
  Adder #(.width(1)) adder_8 (.a(a[7]), .b(b[7]), .out(Y[7]), .cin(adder_7_cout), .cout(cout));
  xor xor_1 (overflow, adder_7_cout, cout);
endmodule

module LU (
  input  [7:0] a,
  input  [7:0] b,
  input  f2,
  input  f0,
  output [7:0] y
);

  wire [7:0] and_1_out, or_1_out, xor_1_out;

  assign and_1_out = a & b;  // AND_Gate and_1, 8 bits wide
  assign or_1_out = a | b;  // OR_Gate or_1, 8 bits wide
  assign xor_1_out = a ^ b;  // XOR_Gate xor_1, 8 bits wide
  Multiplexer #(.select(2), .width(8)) multiplexer_1 (
    .in0(and_1_out), .in1(or_1_out), .in2(xor_1_out), .in3(b), .out(y), .sel({f2, f0}));  // open: en
endmodule

// R Bank
module Register_Bank (
  input  write,
  input  [7:0] val_in,
  input  [1:0] Addr_1,
  input  [1:0] Addr_3,
  input  [1:0] Addr_2,
  output [7:0] out_1,
  output [7:0] out_2
);

  wire CLK_out, demultiplexer_1_out0, demultiplexer_1_out1, demultiplexer_1_out2, demultiplexer_1_out3;
  wire [7:0] R0_q, R1_q, R2_q, R3_q;

  Clock CLK (.out(CLK_out));
  Demultiplexer #(.select(2)) demultiplexer_1 (
    .out0(demultiplexer_1_out0), .out1(demultiplexer_1_out1), .out2(demultiplexer_1_out2),
    .out3(demultiplexer_1_out3), .in(write), .sel(Addr_3));  // open: en
  Register R0 (.D(val_in), .en(demultiplexer_1_out0), .Q(R0_q), .clk(CLK_out));  // open: clr
  Register R1 (.D(val_in), .en(demultiplexer_1_out1), .Q(R1_q), .clk(CLK_out));  // open: clr
  Register R2 (.D(val_in), .en(demultiplexer_1_out2), .Q(R2_q), .clk(CLK_out));  // open: clr
  Register R3 (.D(val_in), .en(demultiplexer_1_out3), .Q(R3_q), .clk(CLK_out));  // open: clr
  Multiplexer #(.select(2), .width(8)) multiplexer_1 (
    .in0(R0_q), .in1(R1_q), .in2(R2_q), .in3(R3_q), .out(out_1), .sel(Addr_1));  // open: en
  Multiplexer #(.select(2), .width(8)) multiplexer_2 (
    .in0(R0_q), .in1(R1_q), .in2(R2_q), .in3(R3_q), .out(out_2), .sel(Addr_2));  // open: en
endmodule

module Mux (
  input  [5:0] Addr_in,
  output [3:0] opcode
);

  wire [3:0] mux_gates_1_out, mux_gates_2_out, mux_gates_3_out, mux_gates_4_out, mux_gates_5_out,
       mux_gates_6_out;

  Mux_gates mux_gates_1 (.in(4'b0000), .f0(Addr_in[0]), .out(mux_gates_1_out));
  Mux_gates mux_gates_2 (.in(4'b1111), .f0(Addr_in[1]), .out(mux_gates_2_out));
  Mux_gates mux_gates_3 (.in(4'b1111), .f0(Addr_in[2]), .out(mux_gates_3_out));
  Mux_gates mux_gates_4 (.in(4'b1111), .f0(Addr_in[3]), .out(mux_gates_4_out));
  Mux_gates mux_gates_5 (.in(4'b1111), .f0(Addr_in[4]), .out(mux_gates_5_out));
  Mux_gates mux_gates_6 (.in(4'b1111), .f0(Addr_in[5]), .out(mux_gates_6_out));
  assign opcode = mux_gates_1_out | mux_gates_2_out | mux_gates_3_out | mux_gates_4_out | mux_gates_5_out | mux_gates_6_out;  // OR_Gate or_1, 4 bits wide

  // Notes on the sheet:
  //   Load 2 M
  //   add
  //   copy
  //   copy A
  //   Load M
  //   Clear
endmodule

module Mux_gates (
  input  [3:0] in,
  input  f0,
  output [3:0] out
);

  and and_1 (out[0], in[0], f0);
  and and_2 (out[1], in[1], f0);
  and and_3 (out[2], in[2], f0);
  and and_4 (out[3], in[3], f0);
endmodule

module Mux_2 (
  input  [7:0] ALU,
  input  [7:0] Reg,
  input  [7:0] Memory,
  input  [4:0] in_4,
  output [7:0] out
);

  wire or_1_out, or_2_out;
  wire [7:0] mux_2_gates_1_out, mux_2_gates_2_out, mux_2_gates_3_out;

  or or_1 (or_1_out, in_4[4], in_4[3]);
  or or_2 (or_2_out, in_4[2], in_4[0]);
  Mux_2_gates mux_2_gates_1 (.in(ALU), .f0(or_2_out), .out(mux_2_gates_1_out));
  Mux_2_gates mux_2_gates_2 (.in(Reg), .f0(in_4[1]), .out(mux_2_gates_2_out));
  Mux_2_gates mux_2_gates_3 (.in(Memory), .f0(or_1_out), .out(mux_2_gates_3_out));
  assign out = mux_2_gates_1_out | mux_2_gates_2_out | mux_2_gates_3_out;  // OR_Gate or_3, 8 bits wide
endmodule

module Mux_2_gates (
  input  [7:0] in,
  input  f0,
  output [7:0] out
);

  and and_1 (out[0], in[0], f0);
  and and_2 (out[1], in[1], f0);
  and and_3 (out[2], in[2], f0);
  and and_4 (out[3], in[3], f0);
  and and_5 (out[4], in[4], f0);
  and and_6 (out[5], in[5], f0);
  and and_7 (out[6], in[6], f0);
  and and_8 (out[7], in[7], f0);
endmodule

module demux (
  input  [7:0] in,
  input  [4:0] in_2,
  output [7:0] ALU,
  output [7:0] Reg,
  output [7:0] Memory
);

  wire or_1_out, or_2_out;

  or or_1 (or_1_out, in_2[1], in_2[2]);
  or or_2 (or_2_out, in_2[3], in_2[4]);
  demux_gates demux_gates_1 (.in_1(in), .in_2(in_2[0]), .out_3(ALU));
  demux_gates demux_gates_2 (.in_1(in), .in_2(or_1_out), .out_3(Reg));
  demux_gates demux_gates_3 (.in_1(in), .in_2(or_2_out), .out_3(Memory));
endmodule

module demux_gates (
  input  [7:0] in_1,
  input  in_2,
  output [7:0] out_3
);

  and and_1 (out_3[0], in_1[0], in_2);
  and and_2 (out_3[1], in_1[1], in_2);
  and and_3 (out_3[2], in_1[2], in_2);
  and and_4 (out_3[3], in_1[3], in_2);
  and and_5 (out_3[4], in_1[4], in_2);
  and and_6 (out_3[5], in_1[5], in_2);
  and and_7 (out_3[6], in_1[6], in_2);
  and and_8 (out_3[7], in_1[7], in_2);
endmodule
